# Fritzing sketch yonpler (saved by Fritzing 0.9.3b)
breadboards: 2

parts:
  パーツ1 = Arduino Uno (Rev3)
  SW1 = DIP Switch 8 Position [package=dipswitch-08]
  U1 = 3.5mm Audio Jack [package=audio-jack-3.5mm-smd]
  U2 = 3.5mm Audio Jack [package=audio-jack-3.5mm-smd]
  C1 = Ceramic Capacitor [capacitance=0.1µF package="100 mil [THT, multilayer]"]

nets:
  N1: パーツ1.D8, SW1.11
  N2: パーツ1.D9_PWM, C1.0
  N3: パーツ1.D10_PWM/SS, SW1.10
  N4: パーツ1.D11_PWM/MOSI, SW1.9
  GND: パーツ1.GND, SW1.1, SW1.2, SW1.3, SW1.4, SW1.5, SW1.6, SW1.7, SW1.8, U1.SLEEVE, U2.SLEEVE
  N5: パーツ1.D2, U1.LEFT
  N6: パーツ1.D3_PWM, SW1.16
  N7: パーツ1.D4, SW1.15
  N8: パーツ1.D5_PWM, SW1.14
  N9: パーツ1.D6_PWM, SW1.13
  N10: パーツ1.D7, SW1.12
  5V: パーツ1.5V
  N11: U2.RIGHT, U2.LEFT, C1.1
